# Fritzing sketch Hardware wiring sketch (saved by Fritzing 0.9.3b)
breadboards: 1

parts:
  U1 = ESP32-38PinWide [part_number=ESP32-38PinWide]
  A1 = ESP32-S3-WROOM-1-N16R8 dev board
  A2 = MQ-2 breakout
  Part1 = Arduino Uno (Rev3)
  R1 = Resistor [tolerance=±5% resistance=220 package=THT]
  R2 = Resistor [tolerance=±5% resistance=220 package=THT]
  R3 = Resistor [tolerance=±5% resistance=220 package=THT]
  LED1 = LED - 5mm [color="Red (633nm)" package="5 mm [THT]"]

nets:
  N1: U1.GPIO25, A1.Pin_5
  N2: U1.GPIO26, A1.Pin_6
  GND: U1.GND, A1.Pin_22, A1.Pin_24, A1.Pin_44, A2.GND, Part1.GND, R3.Pin_0
  N3: A1.Pin_4, R2.Pin_1, R3.Pin_1
  N4: A1.Pin_40, R1.Pin_0
  VCC: A2.VCC, Part1.5V, LED1.anode
  N5: A2.AO, R2.Pin_0

custom parts:
  ESP32-38PinWide: Generic 38-Pin ESP32 with wide format (only access to one side of pins on a breadboard) based on Stephen Lilley's HiLetgo ESP-WROOM-32 ESP32 ESP-32S Development Board.
  ESP32-S3-WROOM-1-N16R8 dev board: ESP32-S3 WIFI+BLE5.0 Development Board ESP32-S3-WROOM-1-N16R8(16M Flash/8SRAM).
  MQ-2 breakout: MQ-2 gas sensor
